// Logisim project T2.circ as structural Verilog: 4 circuits, main circuit main
// PC
module main (
  output [7:0] out_1,
  output [7:0] out_2,
  output [7:0] out_3,
  output [7:0] out_4
);

  wire brzr, clk, dado, wbreg, WM;
  wire [1:0] multiplexer_3_out, muxrs, muxula, PC_sel;
  wire [2:0] OpULA;
  wire [3:0] dual_port_ram_1_instr, OPcode;
  wire [7:0] adder_1_out, adder_2_out, data, imm, multiplexer_1_out, multiplexer_2_out, multiplexer_4_out,
       multiplexer_5_out, ra, rb, register_1_q, ula_t2_1_c;

  Clock #(.highDuration(2), .lowDuration(2)) clock_1 (.out(clk));
  Multiplexer #(.width(8)) multiplexer_1 (.in0(adder_2_out), .in1(rb), .out(multiplexer_1_out), .sel(brzr));
  Adder adder_1 (.a(register_1_q), .b(imm), .out(adder_1_out));  // open: cin, cout
  Multiplexer #(.select(2), .width(8)) multiplexer_2 (
    .in0(adder_2_out), .in1(adder_1_out), .in2(multiplexer_1_out), .out(multiplexer_2_out), .sel(PC_sel));  // open: in3
  Register register_1 (.D(multiplexer_2_out), .en(1'b1), .clk(clk), .Q(register_1_q));  // open: clr
  Adder adder_2 (.a(register_1_q), .b(8'h1), .out(adder_2_out));  // open: cin, cout
  ROM #(.addrWidth(4), .dataWidth(12)) rom_1 (.addr(OPcode), .data({PC_sel, muxrs, wbreg, muxula, dado, WM, OpULA}));
  dual_port_ram dual_port_ram_1 (
    .addr(rb), .pc(register_1_q), .d(ra), .w(WM), .instr({OPcode, dual_port_ram_1_instr}), .data(data));
  assign imm = {{4{dual_port_ram_1_instr[3]}}, dual_port_ram_1_instr};  // Bit_Extender bit_extender_1
  Multiplexer #(.select(2), .width(2)) multiplexer_3 (
    .in0(dual_port_ram_1_instr[3:2]), .in1(2'b00), .in2(2'b01), .out(multiplexer_3_out), .sel(muxrs));  // open: in3
  Multiplexer #(.width(8)) multiplexer_4 (.in0(ula_t2_1_c), .in1(data), .out(multiplexer_4_out), .sel(dado));
  BREGT2 bregt2_1 (
    .D(multiplexer_4_out), .rs1(multiplexer_3_out), .rs2(dual_port_ram_1_instr[1:0]), .W(wbreg), .CLK(clk),
    .rd(multiplexer_3_out), .A(ra), .reg0(out_1), .reg1(out_2), .B(rb), .reg2(out_3), .reg3(out_4));
  Comparator comparator_1 (.a(ra), .b({8{1'b0}}), .eq(brzr));  // open: gt, lt
  Multiplexer #(.select(2), .width(8)) multiplexer_5 (
    .in0(rb), .in1(imm), .in2(8'ha), .in3(8'h14), .out(multiplexer_5_out), .sel(muxula));
  ULA_T2 ula_t2_1 (.A(ra), .B(multiplexer_5_out), .OpULA(OpULA), .C(ula_t2_1_c));  // open: zero

  // Notes on the sheet:
  //   contents of rom_1 (hex, n*v repeats v):
  //   800 400 90 8 1a4 1c4 1e4 2a4 80 81 82 83 84 85 86 87
endmodule

module ULA_T2 (
  input  [7:0] A,
  input  [7:0] B,
  input  [2:0] OpULA,
  output zero,
  output [7:0] C
);

  wire [7:0] adder_1_out, and_1_out, not_1_out, or_1_out, shifter_1_out, shifter_2_out, subtractor_1_out,
       xor_1_out;

  assign not_1_out = ~B;  // NOT_Gate not_1, 8 bits wide
  assign and_1_out = A & B;  // AND_Gate and_1, 8 bits wide
  assign or_1_out = A | B;  // OR_Gate or_1, 8 bits wide
  assign xor_1_out = A ^ B;  // XOR_Gate xor_1, 8 bits wide
  Adder adder_1 (.a(A), .b(B), .out(adder_1_out));  // open: cin, cout
  Subtractor subtractor_1 (.a(A), .b(B), .out(subtractor_1_out));  // open: bin, bout
  Shifter shifter_1 (.in(A), .\dist (B[2:0]), .out(shifter_1_out));
  Shifter #(.shift("lr")) shifter_2 (.in(A), .\dist (B[2:0]), .out(shifter_2_out));
  Multiplexer #(.select(3), .width(8)) multiplexer_1 (
    .in0(not_1_out), .in1(and_1_out), .in2(or_1_out), .in3(xor_1_out), .in4(adder_1_out),
    .in5(subtractor_1_out), .in6(shifter_1_out), .in7(shifter_2_out), .out(C), .sel(OpULA));
  Comparator comparator_1 (.a({8{1'b0}}), .b(C), .eq(zero));  // open: gt, lt
endmodule

module BREGT2 (
  input  [7:0] D,
  input  [1:0] rs1,
  input  [1:0] rs2,
  input  W,
  input  CLK,
  input  [1:0] rd,
  output [7:0] A,
  output [7:0] reg0,
  output [7:0] reg1,
  output [7:0] B,
  output [7:0] reg2,
  output [7:0] reg3
);

  wire demultiplexer_1_out0, demultiplexer_1_out1, demultiplexer_1_out2, demultiplexer_1_out3;
  wire [7:0] multiplexer_1_out, multiplexer_2_out, multiplexer_3_out, multiplexer_4_out;

  Demultiplexer #(.select(2)) demultiplexer_1 (
    .out0(demultiplexer_1_out0), .out1(demultiplexer_1_out1), .out2(demultiplexer_1_out2),
    .out3(demultiplexer_1_out3), .in(W), .sel(rd));
  Register r0 (.D(multiplexer_1_out), .clk(CLK), .Q(reg0));  // open: en, clr
  Multiplexer #(.width(8)) multiplexer_1 (.in0(reg0), .in1(D), .out(multiplexer_1_out), .sel(demultiplexer_1_out0));
  Register r1 (.D(multiplexer_2_out), .clk(CLK), .Q(reg1));  // open: en, clr
  Multiplexer #(.width(8)) multiplexer_2 (.in0(reg1), .in1(D), .out(multiplexer_2_out), .sel(demultiplexer_1_out1));
  Register r2 (.D(multiplexer_3_out), .clk(CLK), .Q(reg2));  // open: en, clr
  Multiplexer #(.width(8)) multiplexer_3 (.in0(reg2), .in1(D), .out(multiplexer_3_out), .sel(demultiplexer_1_out2));
  Register r3 (.D(multiplexer_4_out), .clk(CLK), .Q(reg3));  // open: en, clr
  Multiplexer #(.width(8)) multiplexer_4 (.in0(reg3), .in1(D), .out(multiplexer_4_out), .sel(demultiplexer_1_out3));
  Multiplexer #(.select(2), .width(8)) multiplexer_5 (
    .in0(reg0), .in1(reg1), .in2(reg2), .in3(reg3), .out(B), .sel(rs2));
  Multiplexer #(.select(2), .width(8)) multiplexer_6 (
    .in0(reg0), .in1(reg1), .in2(reg2), .in3(reg3), .out(A), .sel(rs1));

  // Other names for the same wires on the sheet: vr0[7:0] = reg0; vr1[7:0] = reg1; vr2[7:0] = reg2; vr3[7:0] = reg3
endmodule

module dual_port_ram (
  input  [7:0] addr,
  input  [7:0] pc,
  input  [7:0] d,
  input  w,
  output [7:0] instr,
  output [7:0] data
);

  wire clock_1_out, or_1_out;
  wire [7:0] multiplexer_1_out;

  Clock #(.highDuration(2), .lowDuration(2)) clock_1 (.out(clock_1_out));
  or or_1 (or_1_out, w, clock_1_out);
  Multiplexer #(.width(8)) multiplexer_1 (.in0(addr), .in1(pc), .out(multiplexer_1_out), .sel(clock_1_out));
  RAM #(.asyncread("true")) ram_1 (
    .addr(multiplexer_1_out), .we(or_1_out), .oe(1'b1), .clk(clock_1_out), .din(d), .dout(data));
  Register #(.trigger("falling")) pcbuf (.D(data), .en(1'b1), .clk(clock_1_out), .Q(instr));  // open: clr
endmodule
