// Logisim project bregT2.circ as structural Verilog: 4 circuits, main circuit main
// PC
module main (
  output [3:0] acc,
  output [3:0] a0,
  output [3:0] t0,
  output [3:0] t1,
  output [3:0] t2,
  output [3:0] t3,
  output [3:0] t4
);

  wire acc_t, bne, clk, muxula, rd, wbreg;
  wire [1:0] PC_sel;
  wire [2:0] multiplexer_3_out, multiplexer_4_out, OpULA;
  wire [3:0] adder_1_out, adder_2_out, adder_3_out, adder_4_out, adder_5_out, breg8_1_p2, breg8_1_p7, imm,
       multiplexer_1_out, multiplexer_2_out, multiplexer_5_out, OPcode, PC_q;
  wire [11:0] rom_2_data;

  Multiplexer #(.width(4)) multiplexer_1 (.in0(adder_4_out), .in1(adder_5_out), .out(multiplexer_1_out), .sel(bne));
  Multiplexer #(.select(2), .width(4)) multiplexer_2 (
    .in0(adder_4_out), .in1(adder_2_out), .in2(multiplexer_1_out), .out(multiplexer_2_out), .sel(PC_sel));  // open: in3
  Adder #(.width(4)) adder_1 (.a(imm), .b(4'b1100), .out(adder_1_out));  // open: cin, cout
  Clock clock_1 (.out(clk));
  Register #(.width(4)) PC (.D(multiplexer_2_out), .en(1'b1), .clk(clk), .Q(PC_q));  // open: clr
  Adder #(.width(4)) adder_2 (.a(PC_q), .b(adder_1_out), .out(adder_2_out));  // open: cin, cout
  ROM #(.addrWidth(4), .dataWidth(9)) rom_1 (.addr(OPcode), .data({PC_sel, rd, wbreg, muxula, OpULA, acc_t}));
  Adder #(.width(4)) adder_3 (.a(imm), .b(4'b0100), .out(adder_3_out));  // open: cin, cout
  ROM #(.addrWidth(4), .dataWidth(16)) rom_2 (.addr(PC_q), .data({OPcode, rom_2_data[11:10], imm, rom_2_data[5:0]}));
  Adder #(.width(4)) adder_4 (.a(PC_q), .b(4'b0001), .out(adder_4_out));  // open: cin, cout
  Adder #(.width(4)) adder_5 (.a(PC_q), .b(adder_3_out), .out(adder_5_out));  // open: cin, cout
  Multiplexer #(.width(3)) multiplexer_3 (.in0(imm[2:0]), .in1(rom_2_data[5:3]), .out(multiplexer_3_out), .sel(rd));
  Multiplexer #(.width(3)) multiplexer_4 (
    .in0(rom_2_data[2:0]), .in1(rom_2_data[5:3]), .out(multiplexer_4_out), .sel(acc_t));
  // breg8 breg8_1: pin names not known; wires that end beside it: multiplexer_4_out, breg8_1_p2, wbreg, multiplexer_3_out, clk, t4, breg8_1_p7, a0, t0, t1, t2, t3
  Register #(.width(4)) register_1 (.D(breg8_1_p7), .en(acc_t), .clk(clk), .Q(acc));  // open: clr
  Comparator #(.width(4)) comparator_1 (.a(breg8_1_p7), .b(acc), .eq(bne));  // open: gt, lt
  Multiplexer #(.width(4)) multiplexer_5 (.in0(acc), .in1(imm), .out(multiplexer_5_out), .sel(muxula));
  ULA ula_1 (.A(breg8_1_p7), .B(multiplexer_5_out), .OpULA(OpULA), .out_5(breg8_1_p2));  // open: zero

  // Notes on the sheet:
  //   contents of rom_1 (hex, n*v repeats v):
  //   100 80 1 0 78 0 0 0 20 22 24 26 28 2a 2c 2e
  //   contents of rom_2 (hex, n*v repeats v):
  //   4188 4010 4058 4060 2000 141 2010 c103 2018 c080 2020 c0c0 43c9 12c0 2020 c040
endmodule

module ULA (
  input  [3:0] A,
  input  [3:0] B,
  input  [2:0] OpULA,
  output zero,
  output [3:0] out_5
);

  wire [3:0] adder_1_out, and_1_out, not_1_out, or_1_out, shifter_1_out, shifter_2_out, subtractor_1_out,
       xor_1_out;

  assign not_1_out = ~A;  // NOT_Gate not_1, 4 bits wide
  assign and_1_out = A & B;  // AND_Gate and_1, 4 bits wide
  assign or_1_out = A | B;  // OR_Gate or_1, 4 bits wide
  assign xor_1_out = A ^ B;  // XOR_Gate xor_1, 4 bits wide
  Adder #(.width(4)) adder_1 (.a(A), .b(B), .out(adder_1_out));  // open: cin, cout
  Subtractor #(.width(4)) subtractor_1 (.a(A), .b(B), .out(subtractor_1_out));  // open: bin, bout
  Shifter #(.width(4)) shifter_1 (.in(A), .\dist (B[1:0]), .out(shifter_1_out));
  Shifter #(.shift("lr"), .width(4)) shifter_2 (.in(A), .\dist (B[1:0]), .out(shifter_2_out));
  Multiplexer #(.select(3), .width(4)) multiplexer_1 (
    .in0(not_1_out), .in1(and_1_out), .in2(or_1_out), .in3(xor_1_out), .in4(adder_1_out),
    .in5(subtractor_1_out), .in6(shifter_1_out), .in7(shifter_2_out), .out(out_5), .sel(OpULA));
  Comparator #(.width(4)) comparator_1 (.a(4'b0000), .b(out_5), .eq(zero));  // open: gt, lt
endmodule

module breg8 (
  input  [7:0] D,
  input  [1:0] rs1,
  input  [1:0] rs2,
  input  W,
  input  CLK,
  input  [1:0] rd,
  output [7:0] A,
  output [7:0] B
);

  wire demultiplexer_1_out0, demultiplexer_1_out1, demultiplexer_1_out2, demultiplexer_1_out3;
  wire [7:0] multiplexer_1_out, multiplexer_2_out, multiplexer_3_out, multiplexer_4_out, vr0, vr1, vr2, vr3;

  Demultiplexer #(.select(2)) demultiplexer_1 (
    .out0(demultiplexer_1_out0), .out1(demultiplexer_1_out1), .out2(demultiplexer_1_out2),
    .out3(demultiplexer_1_out3), .in(W), .sel(rd));
  Register r0 (.D(multiplexer_1_out), .clk(CLK), .Q(vr0));  // open: en, clr
  Multiplexer #(.width(8)) multiplexer_1 (.in0(vr0), .in1(D), .out(multiplexer_1_out), .sel(demultiplexer_1_out0));
  Register r1 (.D(multiplexer_2_out), .clk(CLK), .Q(vr1));  // open: en, clr
  Multiplexer #(.width(8)) multiplexer_2 (.in0(vr1), .in1(D), .out(multiplexer_2_out), .sel(demultiplexer_1_out1));
  Register r2 (.D(multiplexer_3_out), .clk(CLK), .Q(vr2));  // open: en, clr
  Multiplexer #(.width(8)) multiplexer_3 (.in0(vr2), .in1(D), .out(multiplexer_3_out), .sel(demultiplexer_1_out2));
  Register r3 (.D(multiplexer_4_out), .clk(CLK), .Q(vr3));  // open: en, clr
  Multiplexer #(.width(8)) multiplexer_4 (.in0(vr3), .in1(D), .out(multiplexer_4_out), .sel(demultiplexer_1_out3));
  Multiplexer #(.select(2), .width(8)) multiplexer_5 (.in0(vr0), .in1(vr1), .in2(vr2), .in3(vr3), .out(B), .sel(rs2));
  Multiplexer #(.select(2), .width(8)) multiplexer_6 (.in0(vr0), .in1(vr1), .in2(vr2), .in3(vr3), .out(A), .sel(rs1));
endmodule

module PC (
  input  Input_Enable,
  input  [3:0] INPT,
  output [3:0] out_3
);

  wire button_1_out, clock_1_out, not_1_out;
  wire [3:0] adder_1_out, controlled_buffer_1_out;

  not not_1 (not_1_out, Input_Enable);
  assign controlled_buffer_1_out = not_1_out ? adder_1_out : 4'bz;  // Controlled_Buffer controlled_buffer_1
  assign controlled_buffer_1_out = Input_Enable ? INPT : 4'bz;  // Controlled_Buffer controlled_buffer_2
  Clock clock_1 (.out(clock_1_out));
  Register #(.width(4)) register_1 (
    .D(controlled_buffer_1_out), .clk(clock_1_out), .Q(out_3), .clr(button_1_out));  // open: en
  Button button_1 (.out(button_1_out));
  Adder #(.width(4)) adder_1 (.a(out_3), .b(4'b0001), .out(adder_1_out));  // open: cin, cout
endmodule
