// Logisim project teste.circ as structural Verilog: 4 circuits, main circuit main
module main (
  input  [7:0] in_1
);

  wire ADD_out, FIN_out, JIN_out, LD_out, LDM_out, NOP_out, SRC_out, SUB_out, XCH_out;

  and NOP (NOP_out, ~in_1[7], ~in_1[6], ~in_1[5], ~in_1[4]);  // AND_Gate
  and SRC (SRC_out, ~in_1[7], ~in_1[6], in_1[5], ~in_1[4], in_1[0]);  // AND_Gate
  and FIN (FIN_out, ~in_1[7], ~in_1[6], in_1[5], in_1[4], ~in_1[0]);  // AND_Gate
  and JIN (JIN_out, ~in_1[7], ~in_1[6], in_1[5], in_1[4], in_1[0]);  // AND_Gate
  and ADD (ADD_out, in_1[7], ~in_1[6], ~in_1[5], ~in_1[4]);  // AND_Gate
  and SUB (SUB_out, in_1[7], ~in_1[6], ~in_1[5], in_1[4]);  // AND_Gate
  and LD (LD_out, in_1[7], ~in_1[6], in_1[5], ~in_1[4]);  // AND_Gate
  and LDM (LDM_out, in_1[7], in_1[6], ~in_1[5], in_1[4]);  // AND_Gate
  and XCH (XCH_out, in_1[7], ~in_1[6], in_1[5], in_1[4]);  // AND_Gate
endmodule

module ULA (
  input  [3:0] A,
  input  [3:0] B,
  output zero,
  output [3:0] out_4
);

  wire [3:0] adder_1_out, and_1_out, not_1_out, or_1_out, shifter_1_out, shifter_2_out, subtractor_1_out,
       xor_1_out;

  assign not_1_out = ~A;  // NOT_Gate not_1, 4 bits wide
  assign and_1_out = A & B;  // AND_Gate and_1, 4 bits wide
  assign or_1_out = A | B;  // OR_Gate or_1, 4 bits wide
  assign xor_1_out = A ^ B;  // XOR_Gate xor_1, 4 bits wide
  Adder #(.width(4)) adder_1 (.a(A), .b(B), .out(adder_1_out));  // open: cin, cout
  Subtractor #(.width(4)) subtractor_1 (.a(A), .b(B), .out(subtractor_1_out));  // open: bin, bout
  Shifter #(.width(4)) shifter_1 (.in(A), .\dist (B[1:0]), .out(shifter_1_out));
  Shifter #(.shift("lr"), .width(4)) shifter_2 (.in(A), .\dist (B[1:0]), .out(shifter_2_out));
  Multiplexer #(.select(3), .width(4)) multiplexer_1 (
    .in0(not_1_out), .in1(and_1_out), .in2(or_1_out), .in3(xor_1_out), .in4(adder_1_out),
    .in5(subtractor_1_out), .in6(shifter_1_out), .in7(shifter_2_out), .out(out_4));  // open: sel
  Comparator #(.width(4)) comparator_1 (.a(4'b0000), .b(out_4), .eq(zero));  // open: gt, lt
endmodule

module breg8 (
  input  [2:0] rs1,
  input  [3:0] D,
  input  [2:0] rs2,
  input  [3:0] A,
  input  [3:0] B,
  input  W,
  input  [2:0] rd,
  input  CLK
);

  wire demultiplexer_1_out1, demultiplexer_1_out2, demultiplexer_1_out3, demultiplexer_1_out4,
       demultiplexer_1_out5, demultiplexer_1_out6, demultiplexer_1_out7;
  wire [3:0] multiplexer_1_out, multiplexer_2_out, multiplexer_3_out, multiplexer_4_out, multiplexer_5_out,
       multiplexer_6_out, multiplexer_7_out, vr1, vr2, vr3, vr4, vr5, vr6, vr7;

  Demultiplexer #(.select(3)) demultiplexer_1 (
    .out1(demultiplexer_1_out1), .out2(demultiplexer_1_out2), .out3(demultiplexer_1_out3),
    .out4(demultiplexer_1_out4), .out5(demultiplexer_1_out5), .out6(demultiplexer_1_out6),
    .out7(demultiplexer_1_out7), .in(W), .sel(rd));  // open: out0
  Register #(.width(4)) r1 (.D(multiplexer_1_out), .clk(CLK), .Q(vr1));  // open: en, clr
  Multiplexer #(.width(4)) multiplexer_1 (.in0(vr1), .in1(D), .out(multiplexer_1_out), .sel(demultiplexer_1_out1));
  Register #(.width(4)) r2 (.D(multiplexer_2_out), .clk(CLK), .Q(vr2));  // open: en, clr
  Multiplexer #(.width(4)) multiplexer_2 (.in0(vr2), .in1(D), .out(multiplexer_2_out), .sel(demultiplexer_1_out2));
  Register #(.width(4)) r3 (.D(multiplexer_3_out), .clk(CLK), .Q(vr3));  // open: en, clr
  Multiplexer #(.width(4)) multiplexer_3 (.in0(vr3), .in1(D), .out(multiplexer_3_out), .sel(demultiplexer_1_out3));
  Register #(.width(4)) r4 (.D(multiplexer_4_out), .clk(CLK), .Q(vr4));  // open: en, clr
  Multiplexer #(.width(4)) multiplexer_4 (.in0(vr4), .in1(D), .out(multiplexer_4_out), .sel(demultiplexer_1_out4));
  Register #(.width(4)) r5 (.D(multiplexer_5_out), .clk(CLK), .Q(vr5));  // open: en, clr
  Multiplexer #(.width(4)) multiplexer_5 (.in0(vr5), .in1(D), .out(multiplexer_5_out), .sel(demultiplexer_1_out5));
  Register #(.width(4)) r6 (.D(multiplexer_6_out), .clk(CLK), .Q(vr6));  // open: en, clr
  Multiplexer #(.width(4)) multiplexer_6 (.in0(vr6), .in1(D), .out(multiplexer_6_out), .sel(demultiplexer_1_out6));
  Register #(.width(4)) r7 (.D(multiplexer_7_out), .clk(CLK), .Q(vr7));  // open: en, clr
  Multiplexer #(.width(4)) multiplexer_7 (.in0(vr7), .in1(D), .out(multiplexer_7_out), .sel(demultiplexer_1_out7));
  Multiplexer #(.select(3), .width(4)) multiplexer_8 (
    .in0(4'b0000), .in1(vr1), .in2(vr2), .in3(vr3), .in4(vr4), .in5(vr5), .in6(vr6), .in7(vr7), .out(A),
    .sel(rs1));
  Multiplexer #(.select(3), .width(4)) multiplexer_9 (
    .in0(4'b0000), .in1(vr1), .in2(vr2), .in3(vr3), .in4(vr4), .in5(vr5), .in6(vr6), .in7(vr7), .out(B),
    .sel(rs2));
endmodule

module PC (
  input  Input_Enable,
  input  [3:0] INPT,
  output [3:0] out_3
);

  wire button_1_out, clock_1_out, not_1_out;
  wire [3:0] adder_1_out, controlled_buffer_1_out;

  not not_1 (not_1_out, Input_Enable);
  assign controlled_buffer_1_out = not_1_out ? adder_1_out : 4'bz;  // Controlled_Buffer controlled_buffer_1
  assign controlled_buffer_1_out = Input_Enable ? INPT : 4'bz;  // Controlled_Buffer controlled_buffer_2
  Clock clock_1 (.out(clock_1_out));
  Register #(.width(4)) register_1 (
    .D(controlled_buffer_1_out), .clk(clock_1_out), .Q(out_3), .clr(button_1_out));  // open: en
  Button button_1 (.out(button_1_out));
  Adder #(.width(4)) adder_1 (.a(out_3), .b(4'b0001), .out(adder_1_out));  // open: cin, cout
endmodule
