// Logisim project tp_proj.circ as structural Verilog: 4 circuits, main circuit main
// PC
module main (
  output [3:0] a0,
  output [3:0] t0,
  output [3:0] t1,
  output [3:0] t2,
  output [3:0] t3,
  output [3:0] t4
);

  wire blt, clk, muxula, rd, wbreg;
  wire [1:0] PC_sel;
  wire [2:0] multiplexer_3_out, OpULA;
  wire [3:0] adder_1_out, adder_2_out, breg8_1_a, breg8_1_b, imm, multiplexer_1_out, multiplexer_2_out,
       multiplexer_4_out, OPcode, PC_q, ula_1_out_5;
  wire [11:0] rom_2_data;

  Multiplexer #(.width(4)) multiplexer_1 (.in0(adder_1_out), .in1(adder_2_out), .out(multiplexer_1_out), .sel(blt));
  Multiplexer #(.select(2), .width(4)) multiplexer_2 (
    .in0(adder_1_out), .in1(adder_2_out), .in2(multiplexer_1_out), .out(multiplexer_2_out), .sel(PC_sel));  // open: in3
  Clock clock_1 (.out(clk));
  Register #(.width(4)) PC (.D(multiplexer_2_out), .en(1'b1), .clk(clk), .Q(PC_q));  // open: clr
  ROM #(.addrWidth(4)) rom_1 (.addr(OPcode), .data({PC_sel, rd, wbreg, muxula, OpULA}));
  ROM #(.addrWidth(4), .dataWidth(16)) rom_2 (.addr(PC_q), .data({OPcode, rom_2_data[11:10], imm, rom_2_data[5:0]}));
  Adder #(.width(4)) adder_1 (.a(PC_q), .b(4'b0001), .out(adder_1_out));  // open: cin, cout
  Adder #(.width(4)) adder_2 (.a(PC_q), .b(imm), .out(adder_2_out));  // open: cin, cout
  Multiplexer #(.width(3)) multiplexer_3 (.in0(imm[2:0]), .in1(rom_2_data[5:3]), .out(multiplexer_3_out), .sel(rd));
  breg8 breg8_1 (
    .rs1(rom_2_data[2:0]), .D(ula_1_out_5), .rs2(rom_2_data[5:3]), .W(wbreg), .rd(multiplexer_3_out),
    .CLK(clk), .A(breg8_1_a), .a0(a0), .t0(t0), .B(breg8_1_b), .t1(t1), .t2(t2), .t3(t3), .t4(t4));
  Comparator #(.width(4)) comparator_1 (.a(breg8_1_a), .b(breg8_1_b), .lt(blt));  // open: gt, eq
  Multiplexer #(.width(4)) multiplexer_4 (.in0(breg8_1_b), .in1(imm), .out(multiplexer_4_out), .sel(muxula));
  ULA ula_1 (.A(breg8_1_a), .B(multiplexer_4_out), .OpULA(OpULA), .out_5(ula_1_out_5));  // open: zero

  // Notes on the sheet:
  //   contents of rom_1 (hex, n*v repeats v):
  //   80 40 0 0 3c 0 0 0 10 11 12 13 14 15 16 17
  //   contents of rom_2 (hex, n*v repeats v):
  //   4108 4050 8a 1340 4018 4060 40a8 1a9 c19c c0c4 c106 406d 12c0 c044
endmodule

module ULA (
  input  [3:0] A,
  input  [3:0] B,
  input  [2:0] OpULA,
  output zero,
  output [3:0] out_5
);

  wire [3:0] adder_1_out, and_1_out, not_1_out, or_1_out, shifter_1_out, shifter_2_out, subtractor_1_out,
       xor_1_out;

  assign not_1_out = ~A;  // NOT_Gate not_1, 4 bits wide
  assign and_1_out = A & B;  // AND_Gate and_1, 4 bits wide
  assign or_1_out = A | B;  // OR_Gate or_1, 4 bits wide
  assign xor_1_out = A ^ B;  // XOR_Gate xor_1, 4 bits wide
  Adder #(.width(4)) adder_1 (.a(A), .b(B), .out(adder_1_out));  // open: cin, cout
  Subtractor #(.width(4)) subtractor_1 (.a(A), .b(B), .out(subtractor_1_out));  // open: bin, bout
  Shifter #(.width(4)) shifter_1 (.in(A), .\dist (B[1:0]), .out(shifter_1_out));
  Shifter #(.shift("lr"), .width(4)) shifter_2 (.in(A), .\dist (B[1:0]), .out(shifter_2_out));
  Multiplexer #(.select(3), .width(4)) multiplexer_1 (
    .in0(not_1_out), .in1(and_1_out), .in2(or_1_out), .in3(xor_1_out), .in4(adder_1_out),
    .in5(subtractor_1_out), .in6(shifter_1_out), .in7(shifter_2_out), .out(out_5), .sel(OpULA));
  Comparator #(.width(4)) comparator_1 (.a(4'b0000), .b(out_5), .eq(zero));  // open: gt, lt
endmodule

module breg8 (
  input  [2:0] rs1,
  input  [3:0] D,
  input  [2:0] rs2,
  input  W,
  input  [2:0] rd,
  input  CLK,
  output [3:0] A,
  output [3:0] a0,
  output [3:0] t0,
  output [3:0] B,
  output [3:0] t1,
  output [3:0] t2,
  output [3:0] t3,
  output [3:0] t4
);

  wire demultiplexer_1_out1, demultiplexer_1_out2, demultiplexer_1_out3, demultiplexer_1_out4,
       demultiplexer_1_out5, demultiplexer_1_out6, demultiplexer_1_out7;
  wire [3:0] multiplexer_1_out, multiplexer_2_out, multiplexer_3_out, multiplexer_4_out, multiplexer_5_out,
       multiplexer_6_out, multiplexer_7_out, vr7;

  Demultiplexer #(.select(3)) demultiplexer_1 (
    .out1(demultiplexer_1_out1), .out2(demultiplexer_1_out2), .out3(demultiplexer_1_out3),
    .out4(demultiplexer_1_out4), .out5(demultiplexer_1_out5), .out6(demultiplexer_1_out6),
    .out7(demultiplexer_1_out7), .in(W), .sel(rd));  // open: out0
  Register #(.width(4)) r1 (.D(multiplexer_1_out), .clk(CLK), .Q(a0));  // open: en, clr
  Multiplexer #(.width(4)) multiplexer_1 (.in0(a0), .in1(D), .out(multiplexer_1_out), .sel(demultiplexer_1_out1));
  Register #(.width(4)) r2 (.D(multiplexer_2_out), .clk(CLK), .Q(t0));  // open: en, clr
  Multiplexer #(.width(4)) multiplexer_2 (.in0(t0), .in1(D), .out(multiplexer_2_out), .sel(demultiplexer_1_out2));
  Register #(.width(4)) r3 (.D(multiplexer_3_out), .clk(CLK), .Q(t1));  // open: en, clr
  Multiplexer #(.width(4)) multiplexer_3 (.in0(t1), .in1(D), .out(multiplexer_3_out), .sel(demultiplexer_1_out3));
  Register #(.width(4)) r4 (.D(multiplexer_4_out), .clk(CLK), .Q(t2));  // open: en, clr
  Multiplexer #(.width(4)) multiplexer_4 (.in0(t2), .in1(D), .out(multiplexer_4_out), .sel(demultiplexer_1_out4));
  Register #(.width(4)) r5 (.D(multiplexer_5_out), .clk(CLK), .Q(t3));  // open: en, clr
  Multiplexer #(.width(4)) multiplexer_5 (.in0(t3), .in1(D), .out(multiplexer_5_out), .sel(demultiplexer_1_out5));
  Register #(.width(4)) r6 (.D(multiplexer_6_out), .clk(CLK), .Q(t4));  // open: en, clr
  Multiplexer #(.width(4)) multiplexer_6 (.in0(t4), .in1(D), .out(multiplexer_6_out), .sel(demultiplexer_1_out6));
  Register #(.width(4)) r7 (.D(multiplexer_7_out), .clk(CLK), .Q(vr7));  // open: en, clr
  Multiplexer #(.width(4)) multiplexer_7 (.in0(vr7), .in1(D), .out(multiplexer_7_out), .sel(demultiplexer_1_out7));
  Multiplexer #(.select(3), .width(4)) multiplexer_8 (
    .in0(4'b0000), .in1(a0), .in2(t0), .in3(t1), .in4(t2), .in5(t3), .in6(t4), .in7(vr7), .out(A), .sel(rs1));
  Multiplexer #(.select(3), .width(4)) multiplexer_9 (
    .in0(4'b0000), .in1(a0), .in2(t0), .in3(t1), .in4(t2), .in5(t3), .in6(t4), .in7(vr7), .out(B), .sel(rs2));

  // Other names for the same wires on the sheet: vr1[3:0] = a0; vr2[3:0] = t0; vr3[3:0] = t1; vr4[3:0] = t2;
  //   vr5[3:0] = t3; vr6[3:0] = t4
endmodule

module PC (
  input  Input_Enable,
  input  [3:0] INPT,
  output [3:0] out_3
);

  wire button_1_out, clock_1_out, not_1_out;
  wire [3:0] adder_1_out, controlled_buffer_1_out;

  not not_1 (not_1_out, Input_Enable);
  assign controlled_buffer_1_out = not_1_out ? adder_1_out : 4'bz;  // Controlled_Buffer controlled_buffer_1
  assign controlled_buffer_1_out = Input_Enable ? INPT : 4'bz;  // Controlled_Buffer controlled_buffer_2
  Clock clock_1 (.out(clock_1_out));
  Register #(.width(4)) register_1 (
    .D(controlled_buffer_1_out), .clk(clock_1_out), .Q(out_3), .clr(button_1_out));  // open: en
  Button button_1 (.out(button_1_out));
  Adder #(.width(4)) adder_1 (.a(out_3), .b(4'b0001), .out(adder_1_out));  // open: cin, cout
endmodule
